# Fritzing sketch CoRA2024_ElectronicCircuit (saved by Fritzing 0.9.5d)
breadboards: 1

parts:
  Arduino_Nano = Arduino Nano (Rev3.0)
  Left_Motor = DC Motor
  Right_Motor = DC Motor
  M3 = fc-51 [package=THT]
  M4 = fc-51 [package=THT]
  M5 = fc-51 [package=THT]
  M6 = fc-51 [package=THT]
  M7 = fc-51 [package=THT]
  M8 = fc-51 [package=THT]
  M9 = fc-51 [package=THT]
  BAT2 = LIPO-2000mAh [package=lipo-2000]
  U1 = SWITCH_SPDT [package=kps-1290]
  BAT3 = LIPO-2000mAh [package=lipo-2000]
  L293D_Motor_Driver1 = L293D [package=THT]

nets:
  N1: Arduino_Nano.GND, M3.pin2, M4.pin2, M5.pin2, M6.pin2, M7.pin2, M8.pin2, M9.pin2, BAT2.-, BAT3.-, L293D_Motor_Driver1.0V
  N2: Arduino_Nano.D2, L293D_Motor_Driver1.In_1
  N3: Arduino_Nano.D3, L293D_Motor_Driver1.In_2
  N4: Arduino_Nano.D4, L293D_Motor_Driver1.In_3
  N5: Arduino_Nano.D5, L293D_Motor_Driver1.In_4
  N6: Arduino_Nano.D6, L293D_Motor_Driver1.Enable_1
  N7: Arduino_Nano.D7, L293D_Motor_Driver1.Enable_2
  N8: Arduino_Nano.VIN, U1.S, L293D_Motor_Driver1.+Vmotor
  N9: Arduino_Nano.5V, M3.pin3, M4.pin3, M5.pin3, M6.pin3, M7.pin3, M8.pin3, M9.pin3, L293D_Motor_Driver1.+V
  N10: Arduino_Nano.A6, M4.pin1
  N11: Arduino_Nano.A5, M5.pin1
  N12: Arduino_Nano.A4, M6.pin1
  N13: Arduino_Nano.A3, M7.pin1
  N14: Arduino_Nano.A2, M8.pin1
  N15: Arduino_Nano.A1, M9.pin1
  N16: Arduino_Nano.A0, M3.pin1
  N17: Left_Motor.pin_1, L293D_Motor_Driver1.Out_2_(_Controlled_by_Enable_1_)
  N18: Left_Motor.pin_2, L293D_Motor_Driver1.Out_1_(_Controlled_by_Enable_1_)
  N19: Right_Motor.pin_1, L293D_Motor_Driver1.Out_4_(_Controlled_by_Enable_2_)
  N20: Right_Motor.pin_2, L293D_Motor_Driver1.Out_3_(_Controlled_by_Enable_2_)
  N21: BAT2.+, U1.P, BAT3.+

notes:
  Brown: Battery +
  Blue: Battery -
  Red: Arduino +
  Black: Arduino -
